# Fritzing sketch chess-timer (saved by Fritzing 0.9.3b)
breadboards: 1

parts:
  Part1 = Arduino Uno (Rev3)
  R1 = TRIMPOT [package=3386u]
  LCD1 = LCD screen
  R2 = Resistor [tolerance=±5% resistance=220 package="1206 [SMD]"]
  S1 = Pushbutton [package="[SMD]"]
  S2 = Pushbutton [package="[SMD]"]
  S3 = Pushbutton [package="[SMD]"]
  S4 = Pushbutton [package="[SMD]"]
  S5 = Pushbutton [package="[SMD]"]
  R3 = Resistor [tolerance=±5% resistance=10k package="0402 [SMD]"]
  R4 = Resistor [tolerance=±5% resistance=10k package="0402 [SMD]"]
  R5 = Resistor [tolerance=±5% resistance=10k package="0402 [SMD]"]
  R6 = Resistor [tolerance=±5% resistance=10k package="0402 [SMD]"]
  R7 = Resistor [tolerance=±5% resistance=10k package="0402 [SMD]"]
  VCC1 = Battery block 9V
  S6 = Pushbutton [package=THT]

nets:
  N1: Part1.D8, S3.Pin_3, S3.Pin_4, R5.Pin_1
  N2: Part1.D9_PWM, S1.Pin_3, S1.Pin_4, R3.Pin_1
  N3: Part1.D10_PWM/SS, S2.Pin_3, S2.Pin_4, R4.Pin_1
  N4: Part1.D11_PWM/MOSI, LCD1.E
  N5: Part1.D12/MISO, LCD1.RS
  N6: Part1.D2, LCD1.DB7
  N7: Part1.D3_PWM, LCD1.DB6
  N8: Part1.D4, LCD1.DB5
  N9: Part1.D5_PWM, LCD1.DB4
  N10: Part1.D6_PWM, S5.Pin_3, S5.Pin_4, R7.Pin_1
  N11: Part1.D7, S4.Pin_3, S4.Pin_4, R6.Pin_1
  5V: Part1.5V, R1.CCW, LCD1.VDD, LCD1.LED-, R2.Pin_1, S1.Pin_1, S1.Pin_2, S2.Pin_1, S2.Pin_2, S3.Pin_1, S3.Pin_2, S4.Pin_1, S4.Pin_2, S5.Pin_1, S5.Pin_2
  GND: Part1.GND, R1.CW, LCD1.VSS, LCD1.R/W, R3.Pin_0, R4.Pin_0, R5.Pin_0, R6.Pin_0, R7.Pin_0, VCC1.-
  N12: Part1.VIN, S6.leg0
  N13: R1.WIPER, LCD1.V0
  N14: LCD1.LED+, R2.Pin_0
  N15: VCC1.+, S6.leg1

// code stored in the sketch: chess-timer.ino
#include <LiquidCrystal.h>

// Pin naming
#define PLAY_BTN 10
#define MINUS_BTN 9
#define PLUS_BTN 8
#define PLAYER_ONE_BTN 7
#define PLAYER_TWO_BTN 6

LiquidCrystal lcd(12, 11, 5, 4, 3, 2);

// State variables
boolean configModeActive = false;
boolean plusMinusBtnActive = false;
boolean gameIsRunning = false;
boolean playerOneMoves = true;
boolean playBtnActive = false;
boolean playBtnLongPressActive = false;
String playerOneTime = "00:00";
String playerTwoTime = "00:00";
int editPointer = 0;
int playerOneSeconds = 0;
int playerTwoSeconds = 0;
unsigned long prevMillis = 0;
unsigned long playBtnTimer = 0;
unsigned long playBtnLongPressTime = 300;

void setup() {
  Serial.begin(9600);
  // LCD setup
  lcd.begin(16, 2);
  initClockSeconds();
  display();
  
  // Buttons setup
  pinMode(PLAY_BTN, INPUT);
  pinMode(MINUS_BTN, INPUT);
  pinMode(PLUS_BTN, INPUT);
  pinMode(PLAYER_ONE_BTN, INPUT);
  pinMode(PLAYER_TWO_BTN, INPUT);
}

void loop() {
  playBtnTick();
  plusMinusBtnsTick();
  playerOneBtnTick();
  playerTwoBtnTick();
  updateTimer();
  delay(10);
}

void playBtnTick() {
  if (digitalRead(PLAY_BTN) == HIGH) {
    if (playBtnActive == false) {
      playBtnActive = true;
      playBtnTimer = millis();
    }

    if ((millis() - playBtnTimer > playBtnLongPressTime) && (playBtnLongPressActive == false)) {
      playBtnLongPressActive = true;
      changeMode();
    }
  } else {
    if (playBtnActive == true) {
      if (playBtnLongPressActive == true) {
        playBtnLongPressActive = false;
      } else {
        playBtnClicked();
      }
      playBtnActive = false;
    }
  }
}

void playBtnClicked() {
  if (configModeActive) {
  	moveEditPointer(); 
  } else {
    gameIsRunning = !gameIsRunning;
  }
}

void moveEditPointer() {
  editPointer = (editPointer + 1) % 8;
  display();
}

void changeMode() {
  configModeActive = !configModeActive;
  
  if (configModeActive) {
    reset();
  } else {
    initClockSeconds();
  }
  
  display();
}

void reset() {
  gameIsRunning = false;
  playerOneTime = "00:00";
  playerTwoTime = "00:00";
  editPointer = 0;
  playerOneSeconds = 0;
  playerTwoSeconds = 0;
}

void initClockSeconds() {
  playerOneSeconds = timeToSeconds(playerOneTime);
  playerTwoSeconds = timeToSeconds(playerTwoTime);
}

int timeToSeconds(const String& s) {
  return 60 * s.substring(0, 2).toInt() + s.substring(3).toInt();
}

void display() {
  lcd.clear();
  
  if (configModeActive) {
    lcd.setCursor(1, 0);
    lcd.print(playerOneTime);
    
    lcd.setCursor(10, 0);
    lcd.print(playerTwoTime);
    
    lcd.setCursor(cursorOnLcd(), 1);
    lcd.print("^");
  } else {
    lcd.setCursor(0, 0);
    lcd.print("Player1");
    
    lcd.setCursor(9, 0);
    lcd.print("Player2");
    
    lcd.setCursor(1, 1);
    lcd.print(playerOneTime);
    
    lcd.setCursor(10, 1);
    lcd.print(playerTwoTime);
  }
}

int cursorOnLcd() {
  if (editPointer == 0) return 1;
  if (editPointer == 1) return 2;
  if (editPointer == 2) return 4;
  if (editPointer == 3) return 5;
  if (editPointer == 4) return 10;
  if (editPointer == 5) return 11;
  if (editPointer == 6) return 13;
  if (editPointer == 7) return 14;
}

void plusMinusBtnsTick() {
  if (!configModeActive) return;
  
  int minus = digitalRead(MINUS_BTN);
  int plus = digitalRead(PLUS_BTN);
  
  if (minus == HIGH || plus == HIGH) {
    
    if (!plusMinusBtnActive) {
      plusMinusBtnActive = true;
      
      changeCurrentDigitBy(plus == HIGH ? 1 : -1);
    }
  } else {
    plusMinusBtnActive = false;
  }
}

void changeCurrentDigitBy(int add) {
  String& s = editPointer < 4 ? playerOneTime : playerTwoTime;
  int i = editPointer % 4;
  
  if (i > 1) i++;
  s[i] += add;
  if (s[i] > '9') s[i] = '0';
  if (s[i] < '0') s[i] = '9';
  
  if (i == 3 && s[i] > '5') s[i] = '0';
  if (i == 3 && s[i] < '0') s[i] = '5';
  
  display();
}

void playerOneBtnTick() {
  if (digitalRead(PLAYER_ONE_BTN) == HIGH) {
    playerOneMoves = false;
  }
}

void playerTwoBtnTick() {
  if (digitalRead(PLAYER_TWO_BTN) == HIGH) {
    playerOneMoves = true;
  }
}

void updateTimer() {
  if (configModeActive || !gameIsRunning) return;
  
  unsigned long currMillis = millis();
  
  if (currMillis - prevMillis > 1000) {
    prevMillis = currMillis;
    countDown();
  }
}

void countDown() {
  if (playerOneMoves) {
    if (playerOneSeconds > 0) playerOneSeconds--;
    playerOneTime = secondsToTime(playerOneSeconds);
  } else {
    if (playerTwoSeconds > 0) playerTwoSeconds--;
    playerTwoTime = secondsToTime(playerTwoSeconds);
  }
  
  if (playerOneSeconds <= 0 || playerTwoSeconds <= 0) {
    finishGame();
  } else {
    display();
  }
}

void finishGame() {
  lcd.clear();
  lcd.setCursor(0, 0);
  lcd.print(String("Player ") + (playerOneSeconds <= 0 ? "2" : "1") + String(" won!"));
  gameIsRunning = false;
  delay(1000);
  reset();
  display();
}

String secondsToTime(int seconds) {
  int sec = seconds % 60;
  int min = seconds / 60 % 100;
  String s = (sec < 10 ? "0" : "") + String(sec);
  String m = (min < 10 ? "0" : "") + String(min);
  return m + ":" + s;
}
